# Fritzing sketch The Imperial March (saved by Fritzing 0.9.2b)
breadboards: 1

parts:
  Часть1 = Arduino Uno (Rev3)
  LED1 = LED - 5mm [color="Red (633nm)" package="5 mm [THT]"]
  J1 = Piezo Speaker
  R1 = Resistor [tolerance=±5% resistance=220 package=THT]

nets:
  N1: Часть1.D13/SCK, LED1.anode
  N2: Часть1.GND, LED1.cathode, J1.pin1
  N3: Часть1.D3_PWM, R1.Pin_0
  N4: J1.pin2, R1.Pin_1
